# Fritzing sketch MedicalBot1 (saved by Fritzing 0.9.3b)
breadboards: 2

parts:
  FTDI_Module = Adafruit FTDI Friend [part_number="Adafruit #284"]
  ESP32_Cam = ESP32 - CAM
  Prog_Switch = SWITCH_SPDT [package=kps-1290]
  VCC1 = Battery block 9V
  5V_Voltage_regulator = AMS1777 5V regulator module
  J1 = female pin header, 2 pins [form="♀ (female)"]
  J2 = female pin header, 2 pins [form="♀ (female)"]
  J3 = female pin header, 2 pins [form="♀ (female)"]
  J4 = female pin header, 2 pins [form="♀ (female)"]
  J5 = female pin header, 2 pins [form="♀ (female)"]
  J6 = female pin header, 2 pins [form="♀ (female)"]
  J7 = female pin header, 2 pins [form="♀ (female)"]
  J8 = female pin header, 2 pins [form="♀ (female)"]

nets:
  N1: FTDI_Module.GND, ESP32_Cam.GND#7, Prog_Switch.P, 5V_Voltage_regulator.GND-_(output), J1.pin2
  VCC: FTDI_Module.VCC, ESP32_Cam.5V, 5V_Voltage_regulator.VOUT+, J1.pin1
  N2: FTDI_Module.TX, ESP32_Cam.GPIO3_/_RX, J6.pin1
  N3: FTDI_Module.RX, ESP32_Cam.GPIO1_/_TX, J5.pin2
  N4: ESP32_Cam.GPIO4, J3.pin2
  N5: ESP32_Cam.GPIO2, J3.pin1
  N6: ESP32_Cam.GPIO14, J4.pin2
  N7: ESP32_Cam.GPIO15, J4.pin1
  N8: ESP32_Cam.GPIO13, J2.pin2
  N9: ESP32_Cam.GPIO12, J2.pin1
  N10: ESP32_Cam.3.3V, J7.pin2
  N11: ESP32_Cam.GPIO16, J7.pin1
  N12: ESP32_Cam.GPIO0, Prog_Switch.O, J8.pin2
  N13: ESP32_Cam.GND#12, J8.pin1
  N14: ESP32_Cam.3.3V_/_5V_/_P_OUT, J6.pin2
  N15: ESP32_Cam.GND#16, J5.pin1
  N16: VCC1.-, 5V_Voltage_regulator.GND-_(input)
  N17: VCC1.+, 5V_Voltage_regulator.VIN+

custom parts:
  Adafruit FTDI Friend: Long gone are the days of parallel ports and serial ports. Now the USB port reigns supreme! But USB is hard, and you just want to transfer your every-day serial data from a microcontroller to computer. What now? Enter the FTDI Friend! The FTDI Friend is a tweaked out FTDI FT232RL chip adapter. Sure, like the well-known FTDI cable, it can provide power to your project and there are 4 signal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
  ESP32 - CAM: The ESP32-CAM has a very competitive small-size camera module that can operate independently as a minimum system with a footprint of only 27*40.5*4.5mm and a deep sleep current of up to 6mA.
  AMS1777 5V regulator module: AMS1777 5V regulator module source : https://github.com/ShenTengTu/fritzing_parts/tree/master/voltage%20regulator/AMS1117_5V_regulator_module
